# Fritzing sketch Sketch Sketch (saved by Fritzing 0.9.9b)
breadboards: 1

parts:
  Part1 = Arduino Uno (Rev3)
  R1 = Resistor [tolerance=±5% power=0.25 resistance=220 package=THT]
  R2 = Resistor [tolerance=±5% power=0.25 resistance=220 package=THT]
  R3 = Resistor [tolerance=±5% power=0.25 resistance=220 package=THT]
  R4 = Resistor [tolerance=±5% power=0.25 resistance=220 package=THT]
  R5 = Resistor [tolerance=±5% power=0.25 resistance=220 package=THT]
  LED1 = LED - 5mm [color="Red (633nm)" current=0.030 package="5 mm [THT]"]
  LED2 = LED - 5mm [color="Red (633nm)" current=0.030 package="5 mm [THT]"]
  LED3 = LED - 5mm [color="Red (633nm)" current=0.030 package="5 mm [THT]"]
  LED4 = LED - 5mm [color="Red (633nm)" current=0.030 package="5 mm [THT]"]
  LED5 = LED - 5mm [color="Red (633nm)" current=0.030 package="5 mm [THT]"]
  R6 = Rotary Potentiometer (Small) [maximum_resistance=0.1MΩ package=THT]  # not connected

nets:
  N1: Part1.D8, R4.Pin_0
  N2: Part1.D9_PWM, R3.Pin_0
  N3: Part1.D10_PWM/SS, R2.Pin_0
  N4: Part1.D11_PWM/MOSI, R1.Pin_0
  N5: Part1.D7, R5.Pin_0
  N6: Part1.GND, LED1.cathode, LED2.cathode, LED3.cathode, LED4.cathode, LED5.cathode
  N7: R1.Pin_1, LED1.anode
  N8: R2.Pin_1, LED2.anode
  N9: R3.Pin_1, LED3.anode
  N10: R4.Pin_1, LED4.anode
  N11: R5.Pin_1, LED5.anode

notes:
  WIRE LEGEND :
  Red : Power Source + (5v)
  Black : Ground -
  Yellow : Analog Input for potentiometer
  Other : Digital Output for LEDs
